# Fritzing sketch Circuit Design (saved by Fritzing 0.9.3b)

parts:
  Part1 = Arduino Nano (Rev3.0)
  S1 = Pushbutton [package="[THT]"]
  S2 = Pushbutton [package="[THT]"]
  S3 = Pushbutton [package="[THT]"]
  S4 = Pushbutton [package="[THT]"]
  Part2 = Adafruit Analog 2-Axis Joystick [part_number="Adafruit #512"]
  S5 = Round Pushbutton
  S6 = Round Pushbutton
  S13 = SWITCH-DPDT [package=os]
  S14 = SWITCH-DPDT [package=os]
  R1 = Rotary Potentiometer (Small) [maximum_resistance=100kΩ package=THT]
  M1 = RioRand LM2596
  U1 = LIPO-110mAh [package=lipo-110]
  Part3 = NRF24L01+ Breakout Board
  TP1 = TP4056 [chip_label=TP4056 package="DIP (Dual Inline) [THT]"]
  J1 = Piezo Speaker
  R2 = Resistor [tolerance=±5% resistance=390 package=THT]
  LED1 = LED - 5mm [color="Green (555nm)" package="5 mm [THT]"]
  R3 = Resistor [tolerance=±5% resistance=100 package=THT]
  S15 = Pushbutton [package="[THT]"]

nets:
  GND: Part1.GND, S1.Pin_3, S1.Pin_4, S2.Pin_1, S2.Pin_2, S3.Pin_3, S3.Pin_4, S4.Pin_3, Part2.GND, S5.leg1, S6.leg0, S14.5, R1.leg2, M1.Pin_4, Part3.GND, R2.Pin_0, R3.Pin_0, S15.Pin_1, S15.Pin_2
  N1: Part1.D2, Part2.SWITCH
  N2: Part1.D3, S15.Pin_3
  N3: Part1.D4, S5.leg0
  N4: Part1.D5, S6.leg1
  N5: Part1.D6, J1.pin2
  N6: Part1.D7, S14.6
  N7: Part1.D8, Part3.CE
  N8: Part1.D9, Part3.CS
  N9: Part1.D10, LED1.anode
  N10: Part1.D11/MOSI, Part3.MOSI
  N11: Part1.D12/MISO, Part3.MISO
  N12: Part1.VIN, M1.Pin_3
  5V: Part1.5V, Part2.VCC, R1.leg1
  N13: Part1.A7, Part2.YOUT
  N14: Part1.A6, Part2.XOUT
  N15: Part1.A5, S4.Pin_1, S4.Pin_2
  N16: Part1.A4, S1.Pin_1, S1.Pin_2
  N17: Part1.A3, S2.Pin_3, S2.Pin_4
  N18: Part1.A2, S3.Pin_1, S3.Pin_2
  N19: Part1.A1, R1.wiper
  N20: Part1.A0, S13.3, M1.Pin_1
  3V3: Part1.3V3, Part3.VCC
  N21: Part1.D13/SCK, Part3.SCK
  N22: S13.2, TP1.pin3
  N23: M1.Pin_2, TP1.pin6
  N24: U1.+, TP1.pin4
  N25: U1.-, TP1.pin5
  N26: J1.pin1, R2.Pin_1
  N27: LED1.cathode, R3.Pin_1

notes:
  3.5v - 4.2v
  6v
  3.3v
  5v
  vcc
  gnd
  miso
  sck
  mosi
  csn
  ce

custom parts:
  Adafruit Analog 2-Axis Joystick: This mini-kit makes it easy to mount a PSP/Xbox-like thumb joystick to your project. The thumbstick is an analog joystick - more accurate and sensitive than just 'directional' joysticks - with a 'press in to select' button. Since it's analog, you'll need two analog reading pins on your microcontroller to determine X and Y. Having an extra digital input will let you read the switch. The pack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
  TP4056: A DIP stand-in part for whatever IC you want. With 6 pins on a 300mil dual inline package (DIP) footprint.
